# Fritzing sketch OPT101_Arduino_Wiring1 (saved by Fritzing 0.9.3b)

parts:
  IC1 = IC, SIP package, 6 pins [chip_label=OPT101]
  Part1 = Arduino Nano (Rev3.0)

nets:
  N1: IC1.pin1, Part1.5V
  N2: IC1.pin2, IC1.pin3, Part1.A1
  N3: IC1.pin5, IC1.pin6, Part1.GND
